# Fritzing sketch computer-power-supply (saved by Fritzing 0.9.3b)
breadboards: 1

parts:
  F1 = Resettable Fuse PTC [package=0603]
  D1 = Rectifier Diode [part_number=1N4001 package="300 mil [THT]"]
  D2 = Rectifier Diode [part_number=1N4001 package="300 mil [THT]"]
  D3 = Rectifier Diode [part_number=1N4001 package="300 mil [THT]"]
  D4 = Rectifier Diode [part_number=1N4001 package="300 mil [THT]"]
  V1 = AC Power
  C5 = Electrolytic Capacitor [capacitance=4.7µF package="100 mil [THT, electrolytic]"]

nets:
  Can be replaced with breaker or non-resettable fuse: F1.1, V1.V+
  Investigate: 4001 is too low voltage rating // 4005 or 4006 was suggested/The 1n-400x are also only good for 1amp max current: F1.2, D1.anode, D2.anode, D3.cathode, D4.cathode, V1.V-
  LOAD/VERIFY: Capacitance: D1.cathode, D2.cathode, D3.anode, D4.anode, C5.-, C5.+

notes:
  Rectification of input
  120/240V DC smooth
  120/240V DC with gabs

custom parts:
  Resettable Fuse PTC: Resettable Fuse PTC Resettable Fuse. Spark Fun Electronics SKU : COM-08357
  AC Power: A generic ac power symbol
